// Logisim project alu.circ as structural Verilog: 10 circuits, main circuit main
module main (
  input  [31:0] X,
  input  [31:0] Y,
  input  [5:0] Switch__S,
  output Signed_Overflow,
  output [31:0] RESULT,
  output Equal
);

  wire addo, multiplexer_3_out, or_1_out, subo;
  wire [31:0] add, \and , bitpal, lfsr, \or , select0, select2, select3, sll, slt, sltu, sra, srl, sub;

  Multiplexer #(.select(2), .width(32), .enable("false")) multiplexer_1 (
    .in0(sll), .in2(add), .out(select0), .sel(Switch__S[5:4]));  // open: in1, in3
  sll sll_1 (.in_1(X), .in_2(Y), .out(sll));
  srl srl_1 (.in_1(X), .in_2(Y), .out(srl));
  sra sra_1 (.in_1(X), .in_2(Y), .out(sra));
  Adder #(.width(32)) adder_1 (.a(X), .b(Y), .out(add), .cout(addo));  // open: cin
  Subtractor #(.width(32)) subtractor_1 (.a(X), .b(Y), .out(sub), .bout(subo));  // open: bin
  or or_1 (or_1_out, addo, subo);
  Multiplexer #(.select(2), .width(32), .enable("false")) multiplexer_2 (
    .in0(srl), .in2(sub), .out(select2), .sel(Switch__S[5:4]));  // open: in1, in3
  Multiplexer #(.select(2), .enable("false")) multiplexer_3 (
    .in0(1'b0), .in1(1'b0), .in2(or_1_out), .in3(1'b0), .out(multiplexer_3_out), .sel(Switch__S[5:4]));
  \and  and_1 (.in_1(Y), .in_2(X), .out(\and ));
  \or  or_2 (.in_1(Y), .in_2(X), .out(\or ));
  slt slt_1 (.in_1(X), .in_2(Y), .out(slt));
  sltu sltu_1 (.in_1(X), .in_2(Y), .out(sltu));
  bitpal bitpal_1 (.in_1(X), .in_2(Y), .out(bitpal));
  Multiplexer #(.select(4), .enable("false")) multiplexer_4 (
    .in0(multiplexer_3_out), .in1(1'b0), .in2(multiplexer_3_out), .in3(1'b0), .in4(1'b0), .in5(1'b0),
    .in6(1'b0), .in7(1'b0), .in8(1'b0), .in9(1'b0), .in10(1'b0), .in11(1'b0), .in12(1'b0), .in13(1'b0),
    .in14(1'b0), .in15(1'b0), .out(Signed_Overflow), .sel(Switch__S[3:0]));
  Multiplexer #(.select(2), .width(32), .enable("false")) multiplexer_5 (
    .in0(sra), .in2(sub), .out(select3), .sel(Switch__S[5:4]));  // open: in1, in3
  Comparator #(.width(32)) comparator_1 (.a(X), .b(Y), .eq(Equal));  // open: gt, lt
  lfsr lfsr_1 (.in_1(X), .in_2(Y), .out(lfsr));
  Multiplexer #(.select(4), .width(32), .enable("false")) multiplexer_6 (
    .in0(select0), .in1(add), .in2(select2), .in3(select3), .in4(\and ), .in5(\or ), .in10(slt), .in11(sltu),
    .in14(bitpal), .in15(lfsr), .out(RESULT), .sel(Switch__S[3:0]));  // open: in6, in7, in8, in9, in12, in13

  // Other names for the same wires on the sheet: output[31:0] = RESULT; overflow = Signed_Overflow; source1[31:0] = X;
  //   source2[31:0] = Y; lower[3:0] = Switch__S[3:0]; upper[1:0] = Switch__S[5:4]

  // Notes on the sheet:
  //   INPUTS to your circuit
  //   INPUT to your circuit
  //   DON'T CHANGE THE INPUTS AND OUTPUTS! IF YOU DO SO, YOU NEED TO MAKE SURE THE PINS ARE IN THE RIGHT PLACES!
  //   OUTPUTS of your circuit
endmodule

module sll (
  input  [31:0] in_1,
  input  [31:0] in_2,
  output [31:0] out
);

  wire [4:0] bit_extender_1_out;

  Bit_Extender #(.in_width(32), .out_width(5)) bit_extender_1 (.in(in_2), .out(bit_extender_1_out));
  Shifter #(.width(32)) shifter_1 (.in(in_1), .\dist (bit_extender_1_out), .out(out));
endmodule

module srl (
  input  [31:0] in_1,
  input  [31:0] in_2,
  output [31:0] out
);

  wire [4:0] bit_extender_1_out;

  Bit_Extender #(.in_width(32), .out_width(5)) bit_extender_1 (.in(in_2), .out(bit_extender_1_out));
  Shifter #(.width(32), .shift("lr")) shifter_1 (.in(in_1), .\dist (bit_extender_1_out), .out(out));
endmodule

module sra (
  input  [31:0] in_1,
  input  [31:0] in_2,
  output [31:0] out
);

  wire [4:0] bit_extender_1_out;

  Bit_Extender #(.in_width(32), .out_width(5)) bit_extender_1 (.in(in_2), .out(bit_extender_1_out));
  Shifter #(.width(32), .shift("ar")) shifter_1 (.in(in_1), .\dist (bit_extender_1_out), .out(out));
endmodule

module \and  (
  input  [31:0] in_1,
  input  [31:0] in_2,
  output [31:0] out
);

  assign out = in_1 & in_2;  // AND_Gate and_1, 32 bits wide
endmodule

module \or  (
  input  [31:0] in_1,
  input  [31:0] in_2,
  output [31:0] out
);

  assign out = in_1 | in_2;  // OR_Gate or_1, 32 bits wide
endmodule

module slt (
  input  [31:0] in_1,
  input  [31:0] in_2,
  output [31:0] out
);

  wire comparator_1_lt;

  Comparator #(.width(32)) comparator_1 (.a(in_1), .b(in_2), .lt(comparator_1_lt));  // open: gt, eq
  assign out = {{31{1'b0}}, comparator_1_lt};  // Bit_Extender bit_extender_1
endmodule

module sltu (
  input  [31:0] in_1,
  input  [31:0] in_2,
  output [31:0] out
);

  wire comparator_1_lt;

  Comparator #(.width(32), .mode("unsigned")) comparator_1 (.a(in_1), .b(in_2), .lt(comparator_1_lt));  // open: gt, eq
  assign out = {{31{1'b0}}, comparator_1_lt};  // Bit_Extender bit_extender_1
endmodule

module bitpal (
  input  [31:0] in_1,
  input  [31:0] in_2,
  output [31:0] out
);

  wire comparator_1_eq;

  Comparator #(.width(16)) comparator_1 (
    .a({in_1[0], in_1[1], in_1[2], in_1[3], in_1[4], in_1[5], in_1[6], in_1[7], in_1[8], in_1[9], in_1[10], in_1[11], in_1[12], in_1[13], in_1[14], in_1[15]}),
    .b(in_1[31:16]), .eq(comparator_1_eq));  // open: gt, lt
  assign out = {{31{1'b0}}, comparator_1_eq};  // Bit_Extender bit_extender_1
endmodule

module lfsr (
  input  [31:0] in_1,
  input  [31:0] in_2,
  output [31:0] out
);

  wire xor_1_out, xor_2_out, xor_3_out;
  wire [31:0] bit_extender_1_out, shifter_1_out, shifter_2_out;

  xor xor_1 (xor_1_out, in_1[0], in_1[2]);
  xor xor_2 (xor_2_out, xor_1_out, in_1[3]);
  xor xor_3 (xor_3_out, xor_2_out, in_1[5]);
  Shifter #(.width(32), .shift("lr")) shifter_1 (.in(in_1), .\dist (5'b00001), .out(shifter_1_out));
  assign bit_extender_1_out = {{31{1'b0}}, xor_3_out};  // Bit_Extender bit_extender_1
  Shifter #(.width(32)) shifter_2 (.in(bit_extender_1_out), .\dist ({5{1'b1}}), .out(shifter_2_out));
  assign out = shifter_2_out | shifter_1_out;  // OR_Gate or_1, 32 bits wide
endmodule
