// Logisim project cpu.circ as structural Verilog: 5 circuits, main circuit main
module main (
  input  [31:0] RS_READ_VALUE,
  input  [31:0] RT_READ_VALUE,
  input  [31:0] INSTRUCTION,
  input  CLOCK,
  input  RESET,
  output [31:0] t0,
  output [31:0] t1,
  output [31:0] t2,
  output [31:0] t3,
  output [4:0] RS,
  output [4:0] RT,
  output [4:0] Write_Register,
  output [31:0] RD_WRITE_VALUE,
  output RD_WRITE_ENABLE,
  output [23:0] FETCH_ADDRESS,
  output overflow
);

  wire comparator_2_eq, comparator_3_eq, comparator_4_eq, comparator_5_eq, comparator_6_eq, comparator_7_eq,
       comparator_8_eq, comparator_9_eq, comparator_10_eq, comparator_11_eq, comparator_12_eq,
       comparator_13_eq, comparator_14_eq, comparator_15_eq, comparator_16_eq, determine_register_1_whethert,
       determine_register_2_whethert, itype, jr, jtype, normal_rtype, not_1_out, or_1_out, or_2_out,
       or_3_out, or_4_out, rtype, shift;
  wire [1:0] bit_extender_1_out, bit_extender_2_out, multiplexer_1_out, multiplexer_2_out;
  wire [4:0] rd, shamt, subtractor_1_out, subtractor_2_out;
  wire [5:0] funct, opcode, switch;
  wire [15:0] immediate;
  wire [25:0] address;
  wire [31:0] bit_extender_3_out, bit_extender_4_out, bit_extender_5_out, bit_extender_6_out,
       RegFile_read_data_1, RegFile_read_data_2, rs_value, rt_value, upper, x, y;

  decode_rsrt decode_rsrt_1 (.in_1(INSTRUCTION), .rt(RT), .rs(RS));
  Register #(.width(16)) register_1 ();  // open: D, en, Q, clk, clr
  Subtractor #(.width(5)) subtractor_1 (.a(RT), .b(5'b01000), .out(subtractor_1_out));  // open: bin, bout
  determine_register determine_register_1 (.in_1(RT), .whethert(determine_register_1_whethert));
  determine_register determine_register_2 (.in_1(RS), .whethert(determine_register_2_whethert));
  Subtractor #(.width(5)) subtractor_2 (.a(RS), .b(5'b01000), .out(subtractor_2_out));  // open: bin, bout
  Bit_Extender #(.in_width(5), .out_width(2)) bit_extender_1 (.in(subtractor_1_out), .out(bit_extender_1_out));
  Bit_Extender #(.in_width(5), .out_width(2)) bit_extender_2 (.in(subtractor_2_out), .out(bit_extender_2_out));
  Multiplexer #(.width(2), .enable("false")) multiplexer_1 (
    .in1(bit_extender_1_out), .out(multiplexer_1_out), .sel(determine_register_1_whethert));  // open: in0
  Multiplexer #(.width(2), .enable("false")) multiplexer_2 (
    .in1(bit_extender_2_out), .out(multiplexer_2_out), .sel(determine_register_2_whethert));  // open: in0
  regfile_main RegFile (
    .Read_register_1(multiplexer_2_out), .Read_register_2(multiplexer_1_out), .t0_Value(t0), .t1_Value(t1),
    .t2_Value(t2), .t3_Value(t3), .clock(CLOCK), .Read_Data_1(RegFile_read_data_1),
    .Read_Data_2(RegFile_read_data_2));  // open: write_register, write_data, RegWrite
  Multiplexer #(.width(32), .enable("false")) multiplexer_3 (
    .in0(RS_READ_VALUE), .in1(RegFile_read_data_1), .out(rs_value), .sel(determine_register_2_whethert));
  Multiplexer #(.width(32), .enable("false")) multiplexer_4 (
    .in0(RT_READ_VALUE), .in1(RegFile_read_data_2), .out(rt_value), .sel(determine_register_1_whethert));
  or or_1 (or_1_out, jr, shift);
  Comparator #(.width(6)) comparator_1 (.a(opcode), .b({6{1'b0}}), .eq(rtype));  // open: gt, lt
  Comparator #(.width(6)) comparator_2 (.a(funct), .b(6'b000010), .eq(comparator_2_eq));  // open: gt, lt
  Comparator #(.width(6)) comparator_3 (.a(funct), .b(6'b000011), .eq(comparator_3_eq));  // open: gt, lt
  Comparator #(.width(6)) comparator_4 (.a(funct), .b({6{1'b0}}), .eq(comparator_4_eq));  // open: gt, lt
  Multiplexer #(.width(32), .enable("false")) multiplexer_5 (.in1(rt_value), .out(x), .sel(shift));  // open: in0
  assign bit_extender_3_out = {{27{1'b0}}, shamt};  // Bit_Extender bit_extender_3
  not not_1 (not_1_out, or_1_out);
  Multiplexer #(.width(32), .enable("false")) multiplexer_6 (.in1(rs_value), .out(x), .sel(normal_rtype));  // open: in0
  Multiplexer #(.width(32), .enable("false")) multiplexer_7 (.in1(rt_value), .out(y), .sel(normal_rtype));  // open: in0
  or or_2 (or_2_out, shift, normal_rtype);
  decode decode_1 (
    .in_1(INSTRUCTION), .funct(funct), .shamt(shamt), .rd(rd), .opcode(opcode), .immediate(immediate),
    .address(address));
  or or_3 (or_3_out, comparator_2_eq, comparator_3_eq, comparator_4_eq);
  Multiplexer #(.width(32), .enable("false")) multiplexer_8 (
    .in1(bit_extender_3_out), .out(y), .sel(shift));  // open: in0
  and and_1 (normal_rtype, not_1_out, rtype);
  Multiplexer #(.width(6), .enable("false")) multiplexer_9 (.in1(funct), .out(switch), .sel(or_2_out));  // open: in0
  Comparator #(.width(6)) comparator_5 (.a(funct), .b(6'b001000), .eq(comparator_5_eq));  // open: gt, lt
  and and_2 (shift, or_3_out, rtype);
  and and_3 (jr, comparator_5_eq, rtype);
  Comparator #(.width(6)) comparator_6 (.a(opcode), .b(6'b001001), .eq(comparator_6_eq));  // open: gt, lt
  Comparator #(.width(6)) comparator_7 (.a(opcode), .b(6'b001100), .eq(comparator_7_eq));  // open: gt, lt
  Comparator #(.width(6)) comparator_8 (.a(opcode), .b(6'b001101), .eq(comparator_8_eq));  // open: gt, lt
  Comparator #(.width(6)) comparator_9 (.a(opcode), .b(6'b001001), .eq(comparator_9_eq));  // open: gt, lt
  Comparator #(.width(6)) comparator_10 (.a(opcode), .b(6'b001100), .eq(comparator_10_eq));  // open: gt, lt
  Comparator #(.width(6)) comparator_11 (.a(opcode), .b(6'b001101), .eq(comparator_11_eq));  // open: gt, lt
  Comparator #(.width(6)) comparator_12 (.a(opcode), .b(6'b001001), .eq(comparator_12_eq));  // open: gt, lt
  Comparator #(.width(6)) comparator_13 (.a(opcode), .b(6'b001100), .eq(comparator_13_eq));  // open: gt, lt
  Comparator #(.width(6)) comparator_14 (.a(opcode), .b(6'b001101), .eq(comparator_14_eq));  // open: gt, lt
  Multiplexer #(.width(6), .enable("false")) multiplexer_10 (
    .in1(6'b100001), .out(switch), .sel(comparator_6_eq));  // open: in0
  Multiplexer #(.width(6), .enable("false")) multiplexer_11 (
    .in1(6'b100100), .out(switch), .sel(comparator_7_eq));  // open: in0
  Multiplexer #(.width(6), .enable("false")) multiplexer_12 (
    .in1(6'b100101), .out(switch), .sel(comparator_8_eq));  // open: in0
  Multiplexer #(.width(32), .enable("false")) multiplexer_13 (
    .in1(rs_value), .out(x), .sel(comparator_9_eq));  // open: in0
  Multiplexer #(.width(32), .enable("false")) multiplexer_14 (
    .in1(rs_value), .out(x), .sel(comparator_10_eq));  // open: in0
  Multiplexer #(.width(32), .enable("false")) multiplexer_15 (
    .in1(rs_value), .out(x), .sel(comparator_11_eq));  // open: in0
  Comparator #(.width(6)) comparator_15 (.a(opcode), .b(6'b000010), .eq(comparator_15_eq));  // open: gt, lt
  Comparator #(.width(6)) comparator_16 (.a(opcode), .b(6'b000011), .eq(comparator_16_eq));  // open: gt, lt
  or or_4 (or_4_out, rtype, jtype);
  not not_2 (itype, or_4_out);
  Multiplexer #(.width(32), .enable("false")) multiplexer_16 (
    .in1(bit_extender_4_out), .out(y), .sel(comparator_12_eq));  // open: in0
  assign bit_extender_4_out = {{16{1'b0}}, immediate};  // Bit_Extender bit_extender_4
  assign bit_extender_5_out = {{16{1'b0}}, immediate};  // Bit_Extender bit_extender_5
  Multiplexer #(.width(32), .enable("false")) multiplexer_17 (
    .in1(bit_extender_5_out), .out(y), .sel(comparator_13_eq));  // open: in0
  assign bit_extender_6_out = {{16{1'b0}}, immediate};  // Bit_Extender bit_extender_6
  Multiplexer #(.width(32), .enable("false")) multiplexer_18 (
    .in1(bit_extender_6_out), .out(y), .sel(comparator_14_eq));  // open: in0
  or or_5 (jtype, comparator_15_eq, comparator_16_eq);
  Comparator #(.width(6)) comparator_17 (.a(opcode), .b(6'b001111));  // open: gt, eq, lt
  alu_main ALU (.Switch__S(switch), .X(x), .Signed_Overflow(overflow), .Y(y));  // open: Equal, RESULT
  // mem_main MEM: pin names not known
  write write_1 (.in_1(opcode), .write(RD_WRITE_ENABLE));
  assign upper = {{24{1'b0}}, immediate[15:8]};  // Bit_Extender bit_extender_7

  // Other names for the same wires on the sheet: write = RD_WRITE_ENABLE

  // Notes on the sheet:
  //   These are outputs/inputs from run.circ
  //   These are outputs to run.circ
endmodule

module decode_rsrt (
  input  [31:0] in_1,
  output [4:0] rt,
  output [4:0] rs
);

  wire comparator_1_eq, comparator_2_eq, or_1_out;

  Comparator #(.width(6)) comparator_1 (.a(6'b000010), .b(in_1[31:26]), .eq(comparator_1_eq));  // open: gt, lt
  Comparator #(.width(6)) comparator_2 (.a(6'b000011), .b(in_1[31:26]), .eq(comparator_2_eq));  // open: gt, lt
  Multiplexer #(.width(5), .enable("false")) multiplexer_1 (.in0(in_1[20:16]), .out(rt), .sel(or_1_out));  // open: in1
  Multiplexer #(.width(5), .enable("false")) multiplexer_2 (.in0(in_1[25:21]), .out(rs), .sel(or_1_out));  // open: in1
  or or_1 (or_1_out, comparator_1_eq, comparator_2_eq);
endmodule

module determine_register (
  input  [4:0] in_1,
  output whethert
);

  wire comparator_1_lt, comparator_2_gt;
  wire [4:0] subtractor_1_out;

  Subtractor #(.width(5)) subtractor_1 (.a(in_1), .b(5'b00111), .out(subtractor_1_out));  // open: bin, bout
  Comparator #(.width(5)) comparator_1 (.a(subtractor_1_out), .b(5'b00101), .lt(comparator_1_lt));  // open: gt, eq
  Comparator #(.width(5)) comparator_2 (.a(subtractor_1_out), .b({5{1'b0}}), .gt(comparator_2_gt));  // open: eq, lt
  and and_1 (whethert, comparator_1_lt, comparator_2_gt);
endmodule

module decode (
  input  [31:0] in_1,
  output [5:0] funct,
  output [4:0] shamt,
  output [4:0] rd,
  output [5:0] opcode,
  output [15:0] immediate,
  output [25:0] address
);


  assign address = in_1[25:0];
  assign funct = in_1[5:0];
  assign immediate = in_1[15:0];
  assign opcode = in_1[31:26];
  assign rd = in_1[15:11];
  assign shamt = in_1[10:6];
endmodule

module write (
  input  [5:0] in_1,
  output write
);

  wire comparator_1_eq, comparator_2_eq, comparator_3_eq, comparator_4_eq, comparator_5_eq, or_1_out;

  Comparator #(.width(6)) comparator_1 (.a(in_1), .b(6'b000010), .eq(comparator_1_eq));  // open: gt, lt
  Comparator #(.width(6)) comparator_2 (.a(in_1), .b(6'b000011), .eq(comparator_2_eq));  // open: gt, lt
  Comparator #(.width(6)) comparator_3 (.a(in_1), .b(6'b000100), .eq(comparator_3_eq));  // open: gt, lt
  Comparator #(.width(6)) comparator_4 (.a(in_1), .b(6'b000101), .eq(comparator_4_eq));  // open: gt, lt
  Comparator #(.width(6)) comparator_5 (.a(in_1), .b(6'b001000), .eq(comparator_5_eq));  // open: gt, lt
  not not_1 (write, or_1_out);
  or or_1 (or_1_out, comparator_1_eq, comparator_2_eq, comparator_3_eq, comparator_4_eq, comparator_5_eq);
endmodule
