// Logisim project regfile.circ as structural Verilog: 1 circuit, main circuit main
module main (
  input  [1:0] Read_register_1,
  input  [1:0] Read_register_2,
  input  [1:0] write_register,
  input  [31:0] write_data,
  input  RegWrite,
  input  clock,
  output [31:0] t0_Value,
  output [31:0] t1_Value,
  output [31:0] t2_Value,
  output [31:0] t3_Value,
  output [31:0] Read_Data_1,
  output [31:0] Read_Data_2
);

  wire [31:0] multiplexer_1_out, multiplexer_2_out, multiplexer_3_out, multiplexer_4_out, multiplexer_5_out,
       multiplexer_6_out, multiplexer_7_out, multiplexer_8_out;

  Register #(.width(32)) t0 (.D(multiplexer_1_out), .Q(t0_Value), .clk(clock));  // open: en, clr
  Multiplexer #(.select(2), .width(32), .enable("false")) multiplexer_1 (
    .in0(multiplexer_2_out), .in1(t0_Value), .in2(t0_Value), .in3(t0_Value), .out(multiplexer_1_out),
    .sel(write_register));
  Multiplexer #(.width(32), .enable("false")) multiplexer_2 (
    .in0(t0_Value), .in1(write_data), .out(multiplexer_2_out), .sel(RegWrite));
  Register #(.width(32)) t1 (.D(multiplexer_3_out), .Q(t1_Value), .clk(clock));  // open: en, clr
  Multiplexer #(.select(2), .width(32), .enable("false")) multiplexer_3 (
    .in0(t1_Value), .in1(multiplexer_4_out), .in2(t1_Value), .in3(t1_Value), .out(multiplexer_3_out),
    .sel(write_register));
  Multiplexer #(.width(32), .enable("false")) multiplexer_4 (
    .in0(t1_Value), .in1(write_data), .out(multiplexer_4_out), .sel(RegWrite));
  Register #(.width(32)) t2 (.D(multiplexer_6_out), .Q(t2_Value), .clk(clock));  // open: en, clr
  Multiplexer #(.width(32), .enable("false")) multiplexer_5 (
    .in0(t2_Value), .in1(write_data), .out(multiplexer_5_out), .sel(RegWrite));
  Multiplexer #(.select(2), .width(32), .enable("false")) multiplexer_6 (
    .in0(t2_Value), .in1(t2_Value), .in2(multiplexer_5_out), .in3(t2_Value), .out(multiplexer_6_out),
    .sel(write_register));
  Register #(.width(32)) t3 (.D(multiplexer_7_out), .Q(t3_Value), .clk(clock));  // open: en, clr
  Multiplexer #(.select(2), .width(32), .enable("false")) multiplexer_7 (
    .in0(t3_Value), .in1(t3_Value), .in2(t3_Value), .in3(multiplexer_8_out), .out(multiplexer_7_out),
    .sel(write_register));
  Multiplexer #(.width(32), .enable("false")) multiplexer_8 (
    .in0(t3_Value), .in1(write_data), .out(multiplexer_8_out), .sel(RegWrite));
  Multiplexer #(.select(2), .width(32), .enable("false")) multiplexer_9 (
    .in0(t0_Value), .in1(t1_Value), .in2(t2_Value), .in3(t3_Value), .out(Read_Data_1), .sel(Read_register_1));
  Multiplexer #(.select(2), .width(32), .enable("false")) multiplexer_10 (
    .in0(t0_Value), .in1(t1_Value), .in2(t2_Value), .in3(t3_Value), .out(Read_Data_2), .sel(Read_register_2));

  // Notes on the sheet:
  //   These are INPUTS to the circuit
  //   These are INPUTS to the circuit
  //   DO NOT CHANGE THE LOCATIONS OF THE INPUTS/OUTPUTS! IF YOU DO SO, YOU NEED TO MAKE SURE THE PINS ARE AT THE RIGHT PLACE!
  //   These are OUTPUTS to the circuit
  //   Yet again, the clock is not an actual clock, but an input, one that will be driven from a higher circuit
  //   These are OUTPUTS to the circuit
endmodule
